# Fritzing sketch MMBC Waterslide Timer_Bottom (saved by Fritzing 0.9.9b)
circuit board: 5cm x 3.5cm

parts:
  Arduino_Nano = Arduino Nano (Rev3.0)
  J1 = Screw terminal - 2 pins [package=THT]
  J2 = Screw terminal - 2 pins [package=THT]
  J3 = Screw terminal - 2 pins [package=THT]
  J4 = Screw terminal - 2 pins [package=THT]

nets:
  N1: Arduino_Nano.D2, J1.pin2
  N2: Arduino_Nano.D3, J1.pin1
  N3: Arduino_Nano.GND, J2.pin1
  N4: Arduino_Nano.5V, J2.pin2
  N5: Arduino_Nano.A5, J3.pin1
  N6: Arduino_Nano.A4, J3.pin2
  N7: Arduino_Nano.A1, J4.pin1
  N8: Arduino_Nano.A0, J4.pin2

notes:
  Reset_Button
  Reset_LED
  Start
  Stop
  SDA
  5V
  GND
